# Fritzing sketch ArduinoeMonTXSolar (saved by Fritzing 0.7.7b)
breadboards: 1

parts:
  ATMEGA328 = atmega328 [package=dip]
  XTAL1 = Crystal [frequency="16 Mhz" package=THT]
  C1 = Ceramic Capacitor [capacitance=100nF package="100 mil [THT, multilayer]"]
  C2 = Ceramic Capacitor [capacitance=100nF package="100 mil [THT, multilayer]"]
  C4 = Ceramic Capacitor [capacitance=100nF package="100 mil [THT, multilayer]"]
  C5 = Electrolytic Capacitor [capacitance=47µF voltage=16V package="100 mil [THT, electrolytic]"]
  C6 = Ceramic Capacitor [capacitance=100nF package="100 mil [THT, multilayer]"]
  R1 = Resistor [tolerance=±5% resistance=10k package=THT]
  J1 = male pin header, 6 pins [form="♂ (male)"]
  LED1 = LED - 5mm [color="Red (633nm)" package="5 mm [THT]"]
  R2 = Resistor [tolerance=±5% resistance=220 package=THT]
  OPAMP1 = LM 358 Dual Op-Amp [package="DIP8 [THT]"]
  OPAMP2 = LM 358 Dual Op-Amp [package="DIP8 [THT]"]
  R3 = Resistor [tolerance=±5% resistance=100k package=THT]
  R4 = Resistor [tolerance=±5% resistance=100k package=THT]
  J2 = female pin header, 2 pins [form="♀ (female)"]
  R5 = Resistor [tolerance=±5% resistance=22 package=THT]
  C7 = Electrolytic Capacitor [capacitance=47µF voltage=16V package="100 mil [THT, electrolytic]"]
  R6 = Resistor [tolerance=±5% resistance=6.8k package=THT]
  R7 = Resistor [tolerance=±5% resistance=20k package=THT]
  C8 = Ceramic Capacitor [capacitance=100nF package="100 mil [THT, multilayer]"]
  R8 = Resistor [tolerance=±5% resistance=470k package=THT]
  C9 = Ceramic Capacitor [capacitance=100nF package="100 mil [THT, multilayer]"]
  C10 = Ceramic Capacitor [capacitance=100nF package="100 mil [THT, multilayer]"]
  R9 = Resistor [tolerance=±5% resistance=150k package=THT]
  R10 = Resistor [tolerance=±5% resistance=15k package=THT]
  J3 = female pin header, 2 pins [form="♀ (female)"]
  R11 = Trimmer Potentiometer [maximum_resistance=100kΩ package=THT]
  L1 = Inductor [inductance=10µH package="400 mil [THT]"]
  C12 = Ceramic Capacitor [capacitance=100nF package="100 mil [THT, multilayer]"]
  C11 = Ceramic Capacitor [capacitance=10nF package="200 mil [THT, multilayer]"]
  C13 = Electrolytic Capacitor [capacitance=10µF voltage=16V package="100 mil [THT, electrolytic]"]

nets (from the breadboard view):
  N1: ATMEGA328.RESET, C6.1, R1.Pin_1
  N2: ATMEGA328.D0_(RX), J1.pin3
  N3: ATMEGA328.D1_(TX), J1.pin2
  N4: ATMEGA328.D3_(PWM), OPAMP1.connector0
  N5: ATMEGA328.VCC, C4.1, C5.+, R1.Pin_0, J1.pin4, OPAMP1.connector7, OPAMP2.connector7, R4.Pin_0, C9.0, C10.0, R11.leg1, L1.pin_1
  N6: ATMEGA328.GND, C1.1, C2.0, C4.0, C5.-, J1.pin6, R2.Pin_0, OPAMP1.connector3, OPAMP2.connector3, R3.Pin_1, C8.1, C9.1, C10.1, R11.leg2, C12.1, C11.1, C13.-
  N7: ATMEGA328.XLAT1, XTAL1.pin_1, C2.1
  N8: ATMEGA328.XLAT2, XTAL1.pin_0, C1.0
  N9: ATMEGA328.D13, LED1.anode
  N10: ATMEGA328.AVCC, L1.pin_0, C12.0
  N11: ATMEGA328.AREF, C11.0, C13.+
  N12: ATMEGA328.A2, OPAMP1.connector2, R9.Pin_0, J3.pin1
  N13: ATMEGA328.A3, R7.Pin_0, C8.0
  N14: C6.0, J1.pin1
  N15: LED1.cathode, R2.Pin_1
  N16: OPAMP1.connector1, R11.wiper
  N17: OPAMP2.connector0, OPAMP2.connector1, OPAMP2.connector4, J2.pin2, R5.Pin_1, R9.Pin_1, R10.Pin_0
  N18: OPAMP2.connector2, R3.Pin_0, R4.Pin_1
  N19: OPAMP2.connector5, R6.Pin_1, R8.Pin_1
  N20: OPAMP2.connector6, R7.Pin_1, R8.Pin_0
  N21: J2.pin1, R5.Pin_0, C7.-
  N22: C7.+, R6.Pin_0
  N23: R10.Pin_1, J3.pin2
